// Logisim project Conway-no_autoset.circ as structural Verilog: 1 circuit, main circuit main
module main (
  input  NE2,
  input  E3,
  input  Clock,
  input  Row,
  input  Column,
  input  Lock,
  output State_Out
);

  wire and_1_out, and_2_out, and_3_out, and_4_out, and_5_out, and_6_out, and_7_out, Btn_Invert_out, D_In_q,
       not_1_out, not_2_out, not_3_out, not_4_out, or_1_out, or_2_out, or_3_out;

  Button Btn_Invert (.out(Btn_Invert_out));
  not not_1 (not_1_out, Clock);
  not not_2 (not_2_out, Lock);
  and and_1 (and_1_out, NE2, not_1_out);
  not not_3 (not_3_out, Btn_Invert_out);
  and and_2 (and_2_out, and_1_out, Lock);
  and and_3 (and_3_out, not_2_out, Btn_Invert_out);
  and and_4 (and_4_out, not_3_out, not_2_out);
  and and_5 (and_5_out, not_4_out, not_2_out);
  and and_6 (and_6_out, E3, Lock);
  or or_1 (or_1_out, and_2_out, and_3_out);
  not not_4 (not_4_out, State_Out);
  or or_2 (or_2_out, and_5_out, and_6_out);
  D_Flip_Flop D_In (.D(or_2_out), .clk(or_1_out), .Q(D_In_q));  // open: Qn, preset, reset
  and and_7 (and_7_out, Clock, Lock);
  D_Flip_Flop D_Out (.D(D_In_q), .clk(or_3_out), .Q(State_Out));  // open: Qn, preset, reset
  or or_3 (or_3_out, and_7_out, and_4_out);
  LED led_1 (.in(State_Out));
endmodule
