// Logisim project Conway.circ as structural Verilog: 4 circuits, main circuit conway_cell
module conway_cell (
  input  Set_D_In,
  input  Row,
  input  Column,
  input  Lock,
  input  N1,
  input  N2,
  input  N3,
  input  N4,
  input  N5,
  input  N6,
  input  N7,
  input  N8,
  output Read_D_Out,
  output State_Out
);

  wire adder_1_cout, adder_1_out, adder_2_cout, adder_2_out, adder_3_cout, adder_3_out, adder_4_cout,
       adder_4_out, adder_5_cout, adder_5_out, adder_6_cout, adder_6_out, adder_7_cout, adder_7_out,
       adder_8_cout, adder_8_out, adder_9_cout, adder_9_out, adder_10_cout, adder_10_out, adder_11_cout,
       adder_11_out, Btn_Invert_out, eq_1_e3, eq_1_ne2;

  Button Btn_Invert (.out(Btn_Invert_out));
  Adder #(.width(1)) adder_1 (.a(N1), .b(N2), .out(adder_1_out), .cout(adder_1_cout));  // open: cin
  Adder #(.width(1)) adder_2 (.a(N3), .b(N4), .out(adder_2_out), .cout(adder_2_cout));  // open: cin
  Adder #(.width(1)) adder_3 (.a(N5), .b(N6), .out(adder_3_out), .cout(adder_3_cout));  // open: cin
  Adder #(.width(1)) adder_4 (.a(N7), .b(N8), .out(adder_4_out), .cout(adder_4_cout));  // open: cin
  Adder #(.width(1)) adder_5 (.a(adder_1_out), .b(adder_2_out), .out(adder_5_out), .cout(adder_5_cout));  // open: cin
  Adder #(.width(1)) adder_6 (
    .a(adder_1_cout), .b(adder_2_cout), .out(adder_6_out), .cin(adder_5_cout), .cout(adder_6_cout));
  Adder #(.width(1)) adder_7 (.a(adder_3_out), .b(adder_4_out), .out(adder_7_out), .cout(adder_7_cout));  // open: cin
  Adder #(.width(1)) adder_8 (
    .a(adder_3_cout), .b(adder_4_cout), .out(adder_8_out), .cin(adder_7_cout), .cout(adder_8_cout));
  Adder #(.width(1)) adder_9 (.a(adder_5_out), .b(adder_7_out), .out(adder_9_out), .cout(adder_9_cout));  // open: cin
  Adder #(.width(1)) adder_10 (
    .a(adder_6_out), .b(adder_8_out), .out(adder_10_out), .cin(adder_9_cout), .cout(adder_10_cout));
  Adder #(.width(1)) adder_11 (
    .a(adder_6_cout), .b(adder_8_cout), .out(adder_11_out), .cin(adder_10_cout), .cout(adder_11_cout));
  inner_logic inner_logic_1 (
    .Set_D_In(Set_D_In), .Row(Row), .Column(Column), .NE2(eq_1_ne2), .E3(eq_1_e3), .Lock(Lock),
    .Btn(Btn_Invert_out), .Read_D_Out(Read_D_Out), .State_Out(State_Out));
  LED led_1 (.in(State_Out));
  eq eq_1 (
    .A_LeastSig(adder_9_out), .B(adder_10_out), .C(adder_11_out), .D_MostSig(adder_11_cout), .NE2(eq_1_ne2),
    .E3(eq_1_e3));
endmodule

module inner_logic (
  input  Set_D_In,
  input  Row,
  input  Column,
  input  NE2,
  input  E3,
  input  Lock,
  input  Btn,
  output Read_D_Out,
  output State_Out
);

  wire and_1_out, and_2_out, and_3_out, and_4_out, and_5_out, and_6_out, and_7_out, and_8_out, and_9_out,
       and_10_out, and_11_out, and_12_out, and_14_out, clock_1_out, D_In_q, D_Out_qn, not_1_out, not_2_out,
       not_3_out, not_4_out, or_1_out, or_2_out, or_3_out, or_4_out, or_5_out, or_6_out;

  Clock clock_1 (.out(clock_1_out));
  not not_1 (not_1_out, clock_1_out);
  not not_2 (not_2_out, Lock);
  and and_1 (and_1_out, Row, Column);
  and and_2 (and_2_out, NE2, not_1_out);
  not not_3 (not_3_out, Btn);
  and and_3 (and_3_out, and_1_out, clock_1_out);
  and and_4 (and_4_out, and_2_out, Lock);
  and and_5 (and_5_out, not_2_out, Btn);
  and and_6 (and_6_out, not_3_out, not_2_out);
  and and_7 (and_7_out, D_Out_qn, not_2_out);
  and and_8 (and_8_out, E3, Lock);
  or or_1 (or_1_out, and_4_out, and_5_out);
  and and_9 (and_9_out, Set_D_In, and_1_out);
  not not_4 (not_4_out, and_1_out);
  or or_2 (or_2_out, and_7_out, and_8_out);
  D_Flip_Flop D_In (.D(or_4_out), .clk(or_3_out), .Q(D_In_q));  // open: Qn, preset, reset
  or or_3 (or_3_out, and_3_out, or_1_out);
  and and_10 (and_10_out, clock_1_out, Lock);
  or or_4 (or_4_out, and_9_out, and_11_out);
  and and_11 (and_11_out, not_4_out, or_2_out);
  D_Flip_Flop D_Out (.D(D_In_q), .clk(or_6_out), .Q(State_Out), .Qn(D_Out_qn));  // open: preset, reset
  or or_5 (or_5_out, and_10_out, and_6_out);
  and and_12 (and_12_out, and_1_out, not_1_out);
  and and_13 (Read_D_Out, and_1_out, State_Out);
  and and_14 (and_14_out, not_4_out, or_5_out);
  or or_6 (or_6_out, and_14_out, and_12_out);
endmodule

module eq (
  input  A_LeastSig,
  input  B,
  input  C,
  input  D_MostSig,
  output NE2,
  output E3
);

  wire and_1_out, and_2_out, nor_1_out, not_1_out;

  nor nor_1 (nor_1_out, C, D_MostSig);
  not not_1 (not_1_out, A_LeastSig);
  and and_1 (and_1_out, not_1_out, B);
  and and_2 (and_2_out, A_LeastSig, B);
  nand nand_1 (NE2, and_1_out, nor_1_out);
  and and_3 (E3, and_2_out, nor_1_out);
endmodule

module board_test (
);

  wire Column_sw1, Column_sw2, Column_sw3, conway_cell_1_state_out, conway_cell_2_state_out,
       conway_cell_3_state_out, conway_cell_4_state_out, conway_cell_5_state_out, conway_cell_6_state_out,
       conway_cell_7_state_out, conway_cell_8_state_out, conway_cell_9_state_out, conway_cell_10_state_out,
       D_In_sw1, Lock_sw1, Row_sw1, Row_sw2, Row_sw3, undriven, undriven_2, undriven_3, undriven_4;

  conway_cell conway_cell_1 (
    .Set_D_In(undriven_4), .Row(undriven_3), .Column(undriven_2), .Lock(undriven),
    .State_Out(conway_cell_1_state_out));  // open: N1, N2, N3, N4, N5, N6, N7, N8, Read_D_Out
  LED led_1 (.in(conway_cell_1_state_out));
  DipSwitch #(.number(3)) Row (.sw1(Row_sw1), .sw2(Row_sw2), .sw3(Row_sw3));
  DipSwitch #(.number(3)) Column (.sw1(Column_sw1), .sw2(Column_sw2), .sw3(Column_sw3));
  DipSwitch #(.number(1)) Lock (.sw1(Lock_sw1));
  conway_cell conway_cell_2 (
    .Set_D_In(D_In_sw1), .Row(Row_sw1), .Column(Column_sw1), .Lock(Lock_sw1), .N1(conway_cell_5_state_out),
    .N2(conway_cell_3_state_out), .N3(conway_cell_6_state_out), .State_Out(conway_cell_2_state_out));  // open: N4, N5, N6, N7, N8, Read_D_Out
  conway_cell conway_cell_3 (
    .Set_D_In(D_In_sw1), .Row(Row_sw2), .Column(Column_sw1), .Lock(Lock_sw1), .N1(conway_cell_6_state_out),
    .N2(conway_cell_4_state_out), .N3(conway_cell_7_state_out), .N6(conway_cell_2_state_out),
    .N8(conway_cell_5_state_out), .State_Out(conway_cell_3_state_out));  // open: N4, N5, N7, Read_D_Out
  conway_cell conway_cell_4 (
    .Set_D_In(D_In_sw1), .Row(Row_sw3), .Column(Column_sw1), .Lock(Lock_sw1), .N1(conway_cell_7_state_out),
    .N6(conway_cell_3_state_out), .N8(conway_cell_6_state_out), .State_Out(conway_cell_4_state_out));  // open: N2, N3, N4, N5, N7, Read_D_Out
  DipSwitch #(.number(1)) D_In (.sw1(D_In_sw1));
  LED led_2 (.in(conway_cell_2_state_out));
  LED led_3 (.in(conway_cell_3_state_out));
  LED led_4 (.in(conway_cell_4_state_out));
  conway_cell conway_cell_5 (
    .Set_D_In(D_In_sw1), .Row(Row_sw1), .Column(Column_sw2), .Lock(Lock_sw1), .N1(conway_cell_8_state_out),
    .N2(conway_cell_6_state_out), .N3(conway_cell_9_state_out), .N4(conway_cell_3_state_out),
    .N5(conway_cell_2_state_out), .State_Out(conway_cell_5_state_out));  // open: N6, N7, N8, Read_D_Out
  conway_cell conway_cell_6 (
    .Set_D_In(D_In_sw1), .Row(Row_sw2), .Column(Column_sw2), .Lock(Lock_sw1), .N1(conway_cell_9_state_out),
    .N2(conway_cell_7_state_out), .N3(conway_cell_10_state_out), .N4(conway_cell_4_state_out),
    .N5(conway_cell_3_state_out), .N6(conway_cell_5_state_out), .N7(conway_cell_2_state_out),
    .N8(conway_cell_8_state_out), .State_Out(conway_cell_6_state_out));  // open: Read_D_Out
  conway_cell conway_cell_7 (
    .Set_D_In(D_In_sw1), .Row(Row_sw3), .Column(Column_sw2), .Lock(Lock_sw1), .N1(conway_cell_10_state_out),
    .N5(conway_cell_4_state_out), .N6(conway_cell_6_state_out), .N7(conway_cell_3_state_out),
    .N8(conway_cell_9_state_out), .State_Out(conway_cell_7_state_out));  // open: N2, N3, N4, Read_D_Out
  LED led_5 (.in(conway_cell_5_state_out));
  LED led_6 (.in(conway_cell_6_state_out));
  LED led_7 (.in(conway_cell_7_state_out));
  conway_cell conway_cell_8 (
    .Set_D_In(D_In_sw1), .Row(Row_sw1), .Column(Column_sw3), .Lock(Lock_sw1), .N2(conway_cell_9_state_out),
    .N3(conway_cell_6_state_out), .N5(conway_cell_5_state_out), .State_Out(conway_cell_8_state_out));  // open: N1, N4, N6, N7, N8, Read_D_Out
  conway_cell conway_cell_9 (
    .Set_D_In(D_In_sw1), .Row(Row_sw2), .Column(Column_sw3), .Lock(Lock_sw1), .N2(conway_cell_10_state_out),
    .N4(conway_cell_7_state_out), .N5(conway_cell_6_state_out), .N6(conway_cell_8_state_out),
    .N7(conway_cell_5_state_out), .State_Out(conway_cell_9_state_out));  // open: N1, N3, N8, Read_D_Out
  conway_cell conway_cell_10 (
    .Set_D_In(D_In_sw1), .Row(Row_sw3), .Column(Column_sw3), .Lock(Lock_sw1), .N5(conway_cell_7_state_out),
    .N6(conway_cell_9_state_out), .N7(conway_cell_6_state_out), .State_Out(conway_cell_10_state_out));  // open: N1, N2, N3, N4, N8, Read_D_Out
  LED led_8 (.in(conway_cell_8_state_out));
  LED led_9 (.in(conway_cell_9_state_out));
  LED led_10 (.in(conway_cell_10_state_out));
endmodule
